// Digital circuit cpu.dig as structural Verilog
module cpu (
  input  Clk,
  input  ALUOut,
  input  [15:0] Test,
  input  Enable,
  input  MW,
  input  Reset,
  output Carry,
  output [15:0] Databus,
  output [15:0] Addressbus,
  output [7:0] Opcode,
  output [15:0] PC
);

  wire ARIn, AROut, IRIn, MR, PCIn, PCInc, PCOut, pulldown_1_out, pullup_1_out, pullup_2_out, RegIn;
  wire [1:0] counter_1_out;
  wire [2:0] Ra, Rb, RSel;
  wire [15:0] add_1_s, AR_q, Mem_q, registerfile_1_da, registerfile_1_db;
  wire [15:4] Microcode_d;
  wire [15:14] IR_q;

  PullUp pullup_1 (.out(pullup_1_out));
  Counter #(.Bits(2)) counter_1 (.en(pullup_1_out), .C(Clk), .clr(Reset), .out(counter_1_out));  // open: ovf
  PullUp pullup_2 (.out(pullup_2_out));
  ROM #(.AddrBits(10), .Bits(16)) Microcode (
    .A({Opcode, counter_1_out}), .sel(pullup_2_out),
    .D({Microcode_d[15:9], IRIn, ARIn, AROut, Microcode_d[5:4], MR, PCIn, PCOut, PCInc}));
  PullDown pulldown_1 (.out(pulldown_1_out));
  Register #(.Bits(16)) AR (.D(Databus), .C(Clk), .en(ARIn), .Q(AR_q));
  Register #(.Bits(16)) IR (.D(Databus), .C(Clk), .en(IRIn), .Q({IR_q, Rb, Ra, Opcode}));
  CounterPreset #(.Bits(16), .isProgramCounter("true")) u_PC (
    .en(PCInc), .C(Clk), .dir(pulldown_1_out), .in(Databus), .ld(PCIn), .clr(Reset), .out(PC));  // open: ovf
  LED u_PCInc (.in(PCInc));
  LED u_PCOut (.in(PCOut));
  PullDown #(.Bits(7)) pulldown_2 (.out(Microcode_d[15:9]));
  LED u_PCIn (.in(PCIn));
  LED u_MR (.in(MR));
  PullDown #(.Bits(2)) pulldown_3 (.out(IR_q));
  assign Addressbus = PCOut ? PC : 16'bz;  // Driver driver_1
  LED RaIn (.in(Microcode_d[4]));
  LED RbIn (.in(Microcode_d[5]));
  assign Databus = Enable ? Test : 16'bz;  // Driver driver_2
  assign Addressbus = AROut ? AR_q : 16'bz;  // Driver driver_3
  LED u_AROut (.in(AROut));
  LED u_ARIn (.in(ARIn));
  LED u_IRIn (.in(IRIn));
  PullDown #(.Bits(16)) pulldown_4 (.out(Addressbus));
  PullDown #(.Bits(16)) pulldown_5 (.out(Databus));
  assign Databus = MR ? Mem_q : 16'bz;  // Driver driver_4
  RegisterFile #(.AddrBits(3), .Bits(16)) registerfile_1 (
    .Din(Databus), .we(RegIn), .Rw(RSel), .C(Clk), .Ra(Ra), .Rb(Rb), .Da(registerfile_1_da),
    .Db(registerfile_1_db));
  Multiplexer #(.Bits(3)) multiplexer_1 (.sel(Microcode_d[5]), .in_0(Ra), .in_1(Rb), .out(RSel));
  or or_1 (RegIn, Microcode_d[4], Microcode_d[5]);
  RAMAsync #(.AddrBits(16), .isProgramMemory("true"), .Bits(16)) Mem (.A(Addressbus), .D(Databus), .we(MW), .Q(Mem_q));
  assign Databus = ALUOut ? add_1_s : 16'bz;  // Driver driver_5
  Add #(.Bits(16)) add_1 (.a(registerfile_1_da), .b(registerfile_1_db), .c_i(Clk), .s(add_1_s), .c_o(Carry));

  // Other names for the same wires on the sheet: Decoder[7:0] = Opcode

  // Notes on the sheet:
  //   Test: default 1
  //   contents of Microcode (hex, n*v repeats v):
  //   1,2,3,4
endmodule
